# Fritzing sketch luxo jr (saved by Fritzing 0.9.0b)
circuit board: 8.46667cm x 5.64444cm
breadboards: 1

parts:
  U1 = NodeMCU V1.0
  IC2 = Voltage Regulator [package=78xxl]
  IC3 = Voltage Regulator [package=78xxl]
  J5 = Basic Servo
  J6 = Basic Servo
  J7 = Basic Servo
  J8 = Basic Servo
  LED1 = LED - 3mm [color="Red (633nm)" package="3 mm [THT]"]
  J4 = Basic Servo
  Power_plug1 = Power plug

nets:
  GND: U1.GND, IC2.GND, IC3.GND, J5.gnd, J6.gnd, J7.gnd, J8.gnd, LED1.cathode, J4.gnd, Power_plug1.GND
  N1: U1.D5, LED1.anode
  N2: U1.D6, J8.pulse
  N3: U1.D7, J4.pulse
  N4: U1.D8, J7.pulse
  N5: U1.RX, J5.pulse
  N6: U1.TX, J6.pulse
  N7: U1.Vin, IC3.OUT
  N8: IC2.IN, IC3.IN, Power_plug1.VCC
  VCC: IC2.OUT, J5.vcc, J6.vcc, J7.vcc, J8.vcc, J4.vcc

custom parts:
  NodeMCU V1.0: ESP8266 based NodeMCU
